# Fritzing sketch Rover (saved by Fritzing 0.9.3b)
perfboards: 1

parts:
  LineSensors = female pin header, 8 pins [form="♀ (female)"]
  MotorLeft = female pin header, 2 pins [form="♀ (female)"]
  MotorRight = female pin header, 2 pins [form="♀ (female)"]
  CollisionSensors = female pin header, 4 pins [form="♀ (female)"]
  AVR = Arduino Mega 2560 (Rev3)
  CollisionLights = female pin header, 4 pins [form="♀ (female)"]
  LineLight = female pin header, 1 pin [form="♀ (female)"]
  ABLeft = female pin header, 2 pins [form="♀ (female)"]
  ABRight = female pin header, 2 pins [form="♀ (female)"]
  Raspberry_Pi1 = Raspberry Pi 3 [part_number=RPI-3-V1.2]

nets:
  N1: LineSensors.pin1, AVR.A15
  N2: LineSensors.pin2, AVR.A14
  N3: LineSensors.pin3, AVR.A13
  N4: LineSensors.pin4, AVR.A12
  N5: LineSensors.pin5, AVR.A11
  N6: LineSensors.pin6, AVR.A10
  N7: LineSensors.pin7, AVR.A9
  N8: LineSensors.pin8, AVR.A8
  N9: MotorLeft.pin1, AVR.D5_PWM
  N10: MotorLeft.pin2, AVR.D4_PWM
  N11: MotorRight.pin1, AVR.D6_PWM
  N12: MotorRight.pin2, AVR.D7_PWM
  N13: CollisionSensors.pin1, AVR.A3
  N14: CollisionSensors.pin2, AVR.A2
  N15: CollisionSensors.pin3, AVR.A1
  N16: CollisionSensors.pin4, AVR.A0
  N17: AVR.D19/RX1, ABLeft.pin1
  N18: AVR.D18/TX1, ABLeft.pin2
  N19: AVR.D17_PWM/RX2, ABRight.pin1
  N20: AVR.D16_PWM/TX2, ABRight.pin2
  N21: AVR.D22, CollisionLights.pin4
  N22: AVR.D24, CollisionLights.pin3
  N23: AVR.D26, CollisionLights.pin2
  N24: AVR.D28, CollisionLights.pin1
  N25: AVR.D30, LineLight.pin1
  N26: AVR.D45, Raspberry_Pi1.GPIO22
  N27: AVR.D46, Raspberry_Pi1.GPIO7
  N28: AVR.D47, Raspberry_Pi1.GPIO6
  N29: AVR.D48, Raspberry_Pi1.GPIO5
  N30: AVR.D50, Raspberry_Pi1.GPIO9
  N31: AVR.D51, Raspberry_Pi1.GPIO10
  N32: AVR.D52, Raspberry_Pi1.GPIO11
  N33: AVR.D53, Raspberry_Pi1.GPIO23

notes:
  ReqExc
  AckExc
  DC
  Dir
