# Fritzing sketch Rover (saved by Fritzing 0.9.2b)
perfboards: 1

parts:
  Raspberry_Pi1 = Raspberry Pi 2
  LineSensors = female pin header, 8 pins [form="♀ (female)"]
  MotorLeft = female pin header, 2 pins [form="♀ (female)"]
  MotorRight = female pin header, 2 pins [form="♀ (female)"]
  CollisionSensors = female pin header, 4 pins [form="♀ (female)"]
  Onderdeel1 = Arduino Mega 2560 (Rev3)
  CollisionLights = female pin header, 4 pins [form="♀ (female)"]
  LineLight = female pin header, 1 pin [form="♀ (female)"]
  LCD1 = LCD screen
  ABLeft = female pin header, 2 pins [form="♀ (female)"]
  ABRight = female pin header, 2 pins [form="♀ (female)"]

nets:
  N1: Raspberry_Pi1.GPIO10, Onderdeel1.D51
  N2: Raspberry_Pi1.GPIO9, Onderdeel1.D50
  N3: Raspberry_Pi1.GPIO11, Onderdeel1.D52
  N4: Raspberry_Pi1.GPIO5, Onderdeel1.D48
  N5: Raspberry_Pi1.GPIO6, Onderdeel1.D47
  N6: LineSensors.pin1, Onderdeel1.A15
  N7: LineSensors.pin2, Onderdeel1.A14
  N8: LineSensors.pin3, Onderdeel1.A13
  N9: LineSensors.pin4, Onderdeel1.A12
  N10: LineSensors.pin5, Onderdeel1.A11
  N11: LineSensors.pin6, Onderdeel1.A10
  N12: LineSensors.pin7, Onderdeel1.A9
  N13: LineSensors.pin8, Onderdeel1.A8
  N14: MotorLeft.pin1, Onderdeel1.D5_PWM
  N15: MotorLeft.pin2, Onderdeel1.D4_PWM
  N16: MotorRight.pin1, Onderdeel1.D6_PWM
  N17: MotorRight.pin2, Onderdeel1.D7_PWM
  N18: CollisionSensors.pin1, Onderdeel1.A3
  N19: CollisionSensors.pin2, Onderdeel1.A2
  N20: CollisionSensors.pin3, Onderdeel1.A1
  N21: CollisionSensors.pin4, Onderdeel1.A0
  N22: Onderdeel1.D19/RX1, ABLeft.pin1
  N23: Onderdeel1.D18/TX1, ABLeft.pin2
  N24: Onderdeel1.D2_PWM, ABRight.pin2
  N25: Onderdeel1.D3_PWM, ABRight.pin1
  N26: Onderdeel1.D22, CollisionLights.pin4
  N27: Onderdeel1.D23, CollisionLights.pin3
  N28: Onderdeel1.D24, CollisionLights.pin2
  N29: Onderdeel1.D25, CollisionLights.pin1
  N30: Onderdeel1.D27, LineLight.pin1
  N31: Onderdeel1.D32, LCD1.DB7
  N32: Onderdeel1.D33, LCD1.DB6
  N33: Onderdeel1.D34, LCD1.DB5
  N34: Onderdeel1.D35, LCD1.DB4
  N35: Onderdeel1.D36, LCD1.R/W
  N36: Onderdeel1.D37, LCD1.RS

notes:
  ReqExc
  AckExc
  DC
  Dir
